# Fritzing sketch P1_beacon_jig_PCB (saved by Fritzing 0.9.3b)
circuit board: 2.6cm x 2cm
breadboards: 1

parts:
  J1 = shrouded pin header, 6 pins [form="♂ (shrouded male)"]
  LED1 = smd LED [color="Red (633nm)" package="0805 [SMD]"]
  R1 = Resistor [tolerance=±5% resistance=3.3k package="0805 [SMD]"]
  T2 = Momentary Switch [package=tactile_switch_smd]
  Pad1 = Pad [width=2.1086877651991625 height=2.2151595597484302 connect=center]
  Pad2 = Pad [width=2.2151829895178254 height=2.2790536058700179 connect=center]
  JP1 = Header 2 [package=jst-2-pth]

nets:
  N1: J1.pin3, R1.Pin_1, T2.4
  N2: J1.pin4, Pad1.pad
  N3: J1.pin6, Pad2.pad
  N4: LED1.cathode, R1.Pin_0
  N5: LED1.anode, JP1.1

notes:
  VCC
  GND
  CLK/IO
  P9
  P10
